# Fritzing sketch sketch (saved by Fritzing 0.9.3b)
perfboards: 1

parts:
  Pololu_A1 = Pololu A4988 [package=SO16]
  Raspberry_Pi_Zero1 = Raspberry Pi Zero
  M1 = Stepper Motor - Bipolar
  J2 = Power Jack [package=power_jack_smd]

nets:
  N1: Pololu_A1.RESET, Pololu_A1.SLEEP
  N2: Pololu_A1.STEP, Raspberry_Pi_Zero1.GPIO16
  N3: Pololu_A1.DIR, Raspberry_Pi_Zero1.GPIO21
  N4: Pololu_A1.GND#8, Raspberry_Pi_Zero1.GND
  VDD: Pololu_A1.VDD, Raspberry_Pi_Zero1.5V
  N5: Pololu_A1.1B, M1.D
  N6: Pololu_A1.1A, M1.B
  N7: Pololu_A1.2A, M1.C
  N8: Pololu_A1.2B, M1.A
  N9: Pololu_A1.GND#14, J2.GND
  N10: Pololu_A1.VMOT, J2.GNDBREAK
